// Logisim project cdm16_verilog.circ as structural Verilog: 14 circuits, main circuit cdm16
module cdm16 (
  input  [15:0] data_in,
  input  EXC,
  input  [5:0] exc_vec,
  input  IRQ,
  input  [5:0] int_vec,
  input  clock,
  input  hold,
  output [15:0] SP,
  output [15:0] PC,
  output [15:0] PS,
  output [15:0] address,
  output mem,
  output data_ins_prime,
  output [15:0] R0,
  output rd_wr_prime,
  output [15:0] R1,
  output [15:0] R2,
  output word,
  output [15:0] R3,
  output [15:0] data_out,
  output [15:0] R4,
  output [15:0] R5,
  output [15:0] R6,
  output [15:0] FP,
  output [1:0] status,
  output IAck,
  output fetch
);

  wire alu_asrtD, and_2_out, and_5_out, and_6_out, and_8_out, and_11_out, and_12_out, and_13_out, and_14_out,
       and_19_out, arith_carry, br_rel_nop, clk, clk_inhibit, clk_no_inhibit, comparator_1_eq,
       comparator_3_eq, cout, critical_fault, CUT, d_ff_1_q, d_ff_2_qn, di, double_fault, ei, exc_latch,
       exc_trig_invalid_inst, exc_trig_pc, exc_trig_sp, exc_triggered, halt, inc_address, \int , io_phase,
       jsr, latch_double_fault, latch_int, multiplexer_9_out, nor_1_out, not_1_out, not_2_out, not_3_out,
       not_4_out, not_5_out, not_6_out, not_7_out, or_1_out, or_2_out, or_3_out, or_4_out, or_5_out,
       or_10_out, or_11_out, or_12_out, pc_inc_inhibit, priority_encoder_2_gs, reset_exc, rti, s_r_ff_1_q,
       s_r_ff_2_q, s_r_ff_3_q, startup, virtual_instruction, \wait ;
  wire [2:0] alu_func, alu_op_type, CVZN, exc_internal_vec, multiplexer_1_out, phase, priority_encoder_2_out,
       rd, rs0, rs1, shift_count_d;
  wire [3:0] ps_flags;
  wire [5:0] exc_vec_t;
  wire [9:0] decoder_1_p21;
  wire [15:0] bit_extender_1_out, bit_extender_2_out, bit_extender_3_out, bit_extender_4_out,
       bit_extender_5_out, bus0, bus1, bus_control_1_p2, busD, fetched_instruction, imm, multiplexer_2_out,
       multiplexer_3_out, multiplexer_4_out, multiplexer_5_out, multiplexer_6_out, or_9_out,
       pc_register_1_mon, register_3_q, registers_1_p14, registers_1_p15, registers_1_p16, sp_register_1_mon;
  wire [26:2] dbg_ucommand;
  wire [27:0] multiplexer_10_out, rom_1_data, rom_2_data;

  not not_1 (not_1_out, CUT);
  Register #(.width(6), .trigger("falling")) register_1 (
    .D(exc_vec), .en(EXC), .Q(exc_vec_t), .clk(clk_no_inhibit));  // open: clr
  D_Flip_Flop #(.trigger("low")) d_ff_1 (.clk(clock), .D(hold), .Q(d_ff_1_q));  // open: Qn, preset, en, reset
  S_R_Flip_Flop #(.trigger("falling")) s_r_ff_1 (
    .S(\wait ), .clk(clock), .R(IRQ), .Q(s_r_ff_1_q));  // open: Qn, preset, reset, en
  or or_1 (or_1_out, s_r_ff_2_q, s_r_ff_3_q);
  S_R_Flip_Flop #(.trigger("falling")) s_r_ff_2 (
    .S(halt), .clk(clk_no_inhibit), .R(1'b0), .Q(s_r_ff_2_q));  // open: Qn, preset, reset, en
  S_R_Flip_Flop #(.trigger("falling")) s_r_ff_3 (
    .S(critical_fault), .clk(clk_no_inhibit), .R(1'b0), .Q(s_r_ff_3_q));  // open: Qn, preset, reset, en
  Counter #(.width(3), .max('h7), .trigger("falling")) counter_1 (
    .load(CUT), .D(3'b000), .count(not_1_out), .Q(phase), .clk(clk));  // open: carry, clr
  or or_2 (or_2_out, d_ff_1_q, s_r_ff_1_q, or_1_out);
  not not_2 (not_2_out, or_2_out);
  nor nor_1 (nor_1_out, phase[0], phase[1], phase[2]);
  D_Flip_Flop #(.trigger("falling")) d_ff_2 (
    .clk(clk), .D(d_ff_2_qn), .Qn(d_ff_2_qn), .en(CUT));  // open: Q, preset, reset
  not not_3 (not_3_out, clk_inhibit);
  and and_1 (clk_no_inhibit, clock, not_2_out);
  Priority_Encoder #(.select(2)) priority_encoder_1 (
    .in0(1'b1), .in1(s_r_ff_1_q), .in2(s_r_ff_2_q), .in3(s_r_ff_3_q), .out(status));  // open: gs, en_out, en_in
  and and_2 (and_2_out, startup, clk);
  and and_3 (fetch, nor_1_out, d_ff_2_qn);
  or or_3 (or_3_out, or_4_out, EXC);
  or or_4 (or_4_out, exc_trig_invalid_inst, exc_trig_pc, exc_trig_sp);
  and and_4 (clk, not_3_out, clk_no_inhibit);
  D_Flip_Flop #(.trigger("falling")) d_ff_3 (.clk(and_2_out), .D(CUT), .Qn(startup));  // open: Q, preset, en, reset
  // registers registers_1: pin names not known; wires that end beside it: rs0, rs1, rd, R0, dbg_ucommand[18], R1, clk, R2, R3, R4, R5, R6, FP, registers_1_p14, registers_1_p15, registers_1_p16, busD
  and and_5 (and_5_out, or_4_out, EXC);
  Priority_Encoder priority_encoder_2 (
    .in1(exc_trig_sp), .in2(exc_trig_pc), .in3(exc_trig_invalid_inst), .in7(EXC),
    .out(priority_encoder_2_out), .gs(priority_encoder_2_gs));  // open: in0, in4, in5, in6, en_in, en_out
  and and_6 (and_6_out, or_3_out, exc_latch);
  or or_5 (or_5_out, rti, \int );
  or or_6 (latch_double_fault, and_5_out, and_6_out, or_5_out);
  Multiplexer #(.width(3), .enable("false")) multiplexer_1 (
    .in0(priority_encoder_2_out), .in1(3'b100), .out(multiplexer_1_out), .sel(latch_double_fault));
  Comparator #(.width(3), .mode("unsigned")) comparator_1 (
    .a(exc_internal_vec), .b(3'b111), .eq(comparator_1_eq));  // open: gt, lt
  assign bit_extender_1_out = {{13{1'b0}}, exc_internal_vec};  // Bit_Extender bit_extender_1
  assign bit_extender_2_out = {{10{1'b0}}, exc_vec_t};  // Bit_Extender bit_extender_2
  assign bit_extender_3_out = {{10{1'b0}}, exc_vec};  // Bit_Extender bit_extender_3
  assign bit_extender_4_out = {{13{1'b0}}, 3'b100};  // Bit_Extender bit_extender_4
  Register #(.width(3), .trigger("falling")) register_2 (
    .D(multiplexer_1_out), .en(priority_encoder_2_gs), .Q(exc_internal_vec), .clk(clk_no_inhibit));  // open: clr
  Multiplexer #(.width(16), .enable("false")) multiplexer_2 (
    .in0(bit_extender_1_out), .in1(bit_extender_2_out), .out(multiplexer_2_out), .sel(comparator_1_eq));
  Multiplexer #(.width(16), .enable("false")) multiplexer_3 (
    .in0(bit_extender_3_out), .in1(bit_extender_4_out), .out(multiplexer_3_out), .sel(latch_double_fault));
  and and_7 (IAck, fetch, and_8_out);
  and and_8 (and_8_out, IRQ, PS[15]);
  or or_7 (latch_int, and_8_out, exc_triggered);
  and and_9 (reset_exc, exc_triggered, fetch);
  S_R_Flip_Flop #(.trigger("falling")) s_r_ff_4 (
    .S(priority_encoder_2_gs), .clk(clk_no_inhibit), .R(reset_exc), .Q(exc_latch));  // open: Qn, preset, reset, en
  assign bit_extender_5_out = {{10{1'b0}}, int_vec};  // Bit_Extender bit_extender_5
  Multiplexer #(.width(16), .enable("false")) multiplexer_4 (
    .in0(bit_extender_5_out), .in1(multiplexer_5_out), .out(multiplexer_4_out), .sel(exc_triggered));
  Multiplexer #(.width(16), .enable("false")) multiplexer_5 (
    .in0(multiplexer_2_out), .in1(multiplexer_3_out), .out(multiplexer_5_out), .sel(EXC));
  assign bus0 = dbg_ucommand[15] ? registers_1_p14 : 16'bz;  // Controlled_Buffer controlled_buffer_1
  assign bus1 = dbg_ucommand[16] ? registers_1_p15 : 16'bz;  // Controlled_Buffer controlled_buffer_2
  assign busD = dbg_ucommand[17] ? registers_1_p16 : 16'bz;  // Controlled_Buffer controlled_buffer_3
  Pull_Resistor pull_resistor_1 (.node(busD));
  and and_10 (critical_fault, double_fault, priority_encoder_2_gs);
  or or_8 (exc_triggered, priority_encoder_2_gs, exc_latch);
  assign or_9_out = multiplexer_4_out | 16'h8000;  // OR_Gate or_9, 16 bits wide
  Multiplexer #(.width(16), .enable("false")) multiplexer_6 (
    .in0(busD), .in1(or_9_out), .out(multiplexer_6_out), .sel(latch_int));
  Multiplexer #(.width(16), .enable("false")) multiplexer_7 (
    .in0(multiplexer_6_out), .in1(16'h8200), .out(fetched_instruction), .sel(startup));
  not not_4 (not_4_out, fetch);
  or or_10 (or_10_out, latch_int, startup);
  Pull_Resistor pull_resistor_2 (.node(bus0));
  Pull_Resistor pull_resistor_3 (.node(bus1));
  Register #(.width(16), .trigger("falling")) register_3 (
    .D(fetched_instruction), .en(fetch), .Q(register_3_q), .clk(clk), .clr(and_11_out));
  and and_11 (and_11_out, fetch, not_4_out);
  D_Flip_Flop #(.trigger("falling")) d_ff_4 (
    .clk(clk), .D(or_10_out), .Q(virtual_instruction), .en(fetch));  // open: Qn, preset, reset
  Multiplexer #(.enable("false")) multiplexer_8 (
    .in0(br_rel_nop), .in1(virtual_instruction), .out(pc_inc_inhibit), .sel(exc_triggered));
  assign bus0 = dbg_ucommand[2] ? FP : 16'bz;  // Controlled_Buffer controlled_buffer_4
  assign bus1 = dbg_ucommand[3] ? imm : 16'bz;  // Controlled_Buffer controlled_buffer_5
  assign busD = dbg_ucommand[4] ? imm : 16'bz;  // Controlled_Buffer controlled_buffer_6
  Comparator #(.width(16), .mode("unsigned")) comparator_2 (
    .a(16'h8004), .b(register_3_q), .eq(double_fault));  // open: gt, lt
  // Probe on sp_register_1_mon
  sp_register sp_register_1 (
    .In(busD), .plus_2(dbg_ucommand[24]), .en(dbg_ucommand[25]), .minus_2(dbg_ucommand[23]), .clk(clk),
    .Mon(sp_register_1_mon), .Out(SP));  // open: clr
  assign bus0 = dbg_ucommand[21] ? SP : 16'bz;  // Controlled_Buffer controlled_buffer_7
  assign bus0 = dbg_ucommand[8] ? PC : 16'bz;  // Controlled_Buffer controlled_buffer_8
  // Probe on pc_register_1_mon
  pc_register pc_register_1 (
    .In(busD), .en(dbg_ucommand[11]), .plus_2(and_12_out), .Out(PC), .clk(clk), .Mon(pc_register_1_mon),
    .asrt_inc(and_13_out), .inverse_inc(exc_triggered));  // open: clr
  and and_12 (and_12_out, dbg_ucommand[10], not_5_out);
  and and_13 (and_13_out, jsr, dbg_ucommand[9]);
  // decoder decoder_1: pin names not known; wires that end beside it: register_3_q, ps_flags, {CUT, dbg_ucommand[26:20], rd_wr_prime, dbg_ucommand[18:8], mem, dbg_ucommand[6:2], data_ins_prime, alu_asrtD}, phase, exc_triggered, fetch, jsr, rti, \int , halt, \wait , br_rel_nop, shift_count_d, arith_carry, alu_func, alu_op_type, rs0, rs1, rd, imm, decoder_1_p21
  not not_5 (not_5_out, pc_inc_inhibit);
  assign busD = dbg_ucommand[22] ? SP : 16'bz;  // Controlled_Buffer controlled_buffer_9
  Multiplexer #(.enable("false")) multiplexer_9 (
    .in0(and_14_out), .in1(PS[3]), .out(multiplexer_9_out), .sel(arith_carry));
  // ALU_epty alu_epty_1: pin names not known; wires that end beside it: bus0, bus1, multiplexer_9_out, alu_op_type, alu_func, shift_count_d, address, {cout, CVZN}
  assign busD = dbg_ucommand[9] ? PC : 16'bz;  // Controlled_Buffer controlled_buffer_10
  and and_14 (and_14_out, mem, inc_address);
  assign busD = alu_asrtD ? address : 16'bz;  // Controlled_Buffer controlled_buffer_11
  LED led_1 (.in(PS[15]));
  LED led_2 (.in(clk));
  // Probe on ps_flags
  ps_register ps_register_1 (
    .flags({cout, CVZN}), .word(busD), .clk(clk), .out(PS), .out_flags(ps_flags),
    .latch_flags(dbg_ucommand[13]), .latch_word(dbg_ucommand[14]), .ei(ei), .di(di));
  LED led_3 (.in(clk_no_inhibit));
  assign busD = dbg_ucommand[12] ? PS : 16'bz;  // Controlled_Buffer controlled_buffer_12
  or or_11 (or_11_out, io_phase, clk_inhibit);
  not not_6 (not_6_out, or_11_out);
  and and_15 (word, dbg_ucommand[26], not_6_out);
  Comparator #(.width(28)) comparator_3 (.a({28{1'b0}}), .b(rom_1_data), .eq(comparator_3_eq));  // open: gt, lt
  and and_16 (exc_trig_sp, rom_1_data[25], busD[0]);
  and and_17 (exc_trig_pc, busD[0], rom_1_data[11]);
  ROM #(.addrWidth(10), .dataWidth(28)) rom_1 (.addr(decoder_1_p21), .data(rom_1_data));  // open: sel
  ROM #(.addrWidth(10), .dataWidth(28)) rom_2 (.addr(decoder_1_p21), .data(rom_2_data));  // open: sel
  and and_18 (exc_trig_invalid_inst, comparator_3_eq, not_7_out);
  not not_7 (not_7_out, exc_latch);
  Multiplexer #(.width(28), .enable("false")) multiplexer_10 (
    .in0(rom_1_data), .in1(rom_2_data), .out(multiplexer_10_out), .sel(exc_triggered));
  // verilator_component_1_0_SNAPSHOT_all_bus_control bus_control_1: pin names not known; wires that end beside it: busD, bus_control_1_p2, dbg_ucommand[20], inc_address, address[0], io_phase, dbg_ucommand[26], clk_inhibit, clk_no_inhibit, 1'b0, data_out, data_in
  assign busD = rd_wr_prime ? bus_control_1_p2 : 16'bz;  // Controlled_Buffer controlled_buffer_13
  Multiplexer #(.width(28), .enable("false")) multiplexer_11 (
    .in0(multiplexer_10_out), .in1(28'h8000000),
    .out({CUT, dbg_ucommand[26:20], rd_wr_prime, dbg_ucommand[18:8], mem, dbg_ucommand[6:2], data_ins_prime, alu_asrtD}),
    .sel(or_12_out));
  or or_12 (or_12_out, status[1], startup, and_19_out);
  and and_19 (and_19_out, latch_int, fetch);

  // Other names for the same wires on the sheet: address_out[15:0] = address; busA[15:0] = address; CVZN[3] = cout;
  //   dbg_ucommand (some bits) = {CUT, rd_wr_prime, mem, data_ins_prime, alu_asrtD}; data = data_ins_prime;
  //   fp_asrt0 = dbg_ucommand[2]; imm_asrt1 = dbg_ucommand[3]; imm_asrtD = dbg_ucommand[4];
  //   imm_extend_negative = dbg_ucommand[5]; imm_shift = dbg_ucommand[6]; pc_asrt0 = dbg_ucommand[8];
  //   pc_asrtD = dbg_ucommand[9]; pc_inc = dbg_ucommand[10]; pc_latch = dbg_ucommand[11]; ps_asrtD = dbg_ucommand[12];
  //   ps_latch_flags = dbg_ucommand[13]; ps_latch_word = dbg_ucommand[14]; r_asrt0 = dbg_ucommand[15];
  //   r_asrt1 = dbg_ucommand[16]; r_asrtD = dbg_ucommand[17]; r_latch = dbg_ucommand[18]; read = rd_wr_prime;
  //   sign_extend = dbg_ucommand[20]; sp_asrt0 = dbg_ucommand[21]; sp_asrtD = dbg_ucommand[22];
  //   sp_dec = dbg_ucommand[23]; sp_inc = dbg_ucommand[24]; sp_latch = dbg_ucommand[25]; word_t = dbg_ucommand[26];
  //   direct_exc_vec[5:0] = exc_vec; exc_trig_ext = EXC; pc_value[15:0] = PC; ps_value[15:0] = PS; cin = PS[3];
  //   int_en = PS[15]; sp_value[15:0] = SP

  // Notes on the sheet:
  //   hold: pull=down
  //   clock: pull=down
  //   IRQ: pull=down
  //   data_in: pull=down
  //   EXC: pull=down
  //   0 - running
  //   1 - waiting
  //   2 - halted
  //   3 - fault
  //   3
  //   2
  //   1
  //   int, reset, rti
  //   Double fault: 1. Unrecoverable instruction
  //   2. Multiple exceptions on the same phase
  //   3. Mutiple exceptions across several phases
  //   SP
  //   Coco-de-Mer 16
  //   Designed by Nikolay Repin
  //   2023
  //   PС
  //   CVZN
  //   PS
  //   contents of rom_1 (hex, n*v repeats v):
  //   4*0 4*c000000 4a00282 5280882 ca00282 d280882 ce00082 e280082 ca01082 d284082 ca20082 d2c0082
  //   c0c0580 4a00282 8440000 a020000 8041000 8024000 8040200 8020800 a210001 5*0 804a001 15*0 c0c8082
  //   80c8082 81c8082 c0c8080 80c8080 81c8080 c028082 8028082 8*0 c0c00ce c0c00ee 80c008e 80c00ae 81c008e
  //   81c00ae c0200ce c0200ee 802008e 80200ae 8040010 8040030 804a009 804a029 800a008 800a028 4a01082
  //   4080888 ca00092 ca000b2 a200049 a200069 4a00282 4a00282 8*0 c0d8082 80d8082 81d8082 c0d8080 80d8080
  //   81d8080 c038082 8038082 8*0 c080980 804a001 801a000 805a001 8000949 8000969 8000400 c080580 16*0
  //   c080980 d284082 9*0 8020800 60*0 4a00282 c084088 4*0 8000949 8000969 120*0 4080888 127*0 c084088
  //   contents of rom_2 (hex, n*v repeats v):
  //   4*8000400 4*c000000 4a00282 5280082 4a00282 5280082 4e00082 4280082 4a01082 5280082 4a20082 5280082
  //   c080580 4a00282 400000 20000 1000 20000 200 20000 210001 5*8000400 8001 15*8000400 c088482 8088482
  //   8188482 c088480 8088480 8188480 c028482 8028482 8*8000400 c0804ce c0804ee 808048e 80804ae 818048e
  //   81804ae c0204ce c0204ee 802048e 80204ae 8000410 8000430 800a409 800a429 8008408 8008428 4a01082
  //   4080088 4a00092 4a000b2 8200449 8200469 4a00282 4a00282 8*8000400 c098482 8098482 8198482 c098480
  //   8098480 8198480 c038482 8038482 8*8000400 c080580 8008401 8018400 8018401 8000549 8000569 8000400
  //   c080180 8*0 8*8000400 4080180 5280082 9000400 8800400 9000400 8000400 9000400 8800400 9000400
  //   8800400 8000400 20000 60*8000400 4a00282 4080088 9000400 9000400 8000400 8000400 149 169 32*8000400
  //   8*0 8*8000400 9000400 800000 9*8000400 9000400 60*8000400 4080088 5*8000400 9000400 9000400
  //   32*8000400 8*0 9*8000400 8800400 70*8000400 4080088 39*8000400 8*0 80*8000400 1000000 39*8000400 8*0
  //   80*8000400 9000400 39*8000400 8*0 120*8000400 8*0 120*8000400
endmodule

module sp_register (
  input  [15:0] In,
  input  clr,
  input  clk,
  input  plus_2,
  input  en,
  input  minus_2,
  output [15:0] Out,
  output [15:0] Mon
);

  wire count, en_t;
  wire [15:0] incdec2_1_out, multiplexer_1_out;

  Multiplexer #(.width(16), .disabled(0), .enable("false")) multiplexer_1 (
    .in0(In), .in1(incdec2_1_out), .out(multiplexer_1_out), .sel(count));
  Register #(.width(16), .trigger("falling")) register_1 (
    .D(multiplexer_1_out), .en(en_t), .Q(Mon), .clk(clk), .clr(clr));
  or or_1 (count, plus_2, minus_2);
  or or_2 (en_t, count, en);
  incdec2 incdec2_1 (.in(Mon), .out(incdec2_1_out), .inc_dec_prime(plus_2));
  Multiplexer #(.width(16), .disabled(0), .enable("false")) multiplexer_2 (
    .in0(Mon), .in1(incdec2_1_out), .out(Out), .sel(minus_2));

  // Notes on the sheet:
  //   plus_2: pull=down
  //   clr: pull=down
  //   minus_2: pull=down
  //   en: pull=up
  //   clk: pull=down
endmodule

module pc_register (
  input  [15:0] In,
  input  clr,
  input  clk,
  input  en,
  input  plus_2,
  input  asrt_inc,
  input  inverse_inc,
  output [15:0] Out,
  output [15:0] Mon
);

  wire en_t, not_1_out;
  wire [15:0] incdec2_1_out, multiplexer_1_out;

  Register #(.width(16), .trigger("falling")) register_1 (
    .D(multiplexer_1_out), .en(en_t), .Q(Mon), .clk(clk), .clr(clr));
  Multiplexer #(.width(16), .disabled(0), .enable("false")) multiplexer_1 (
    .in0(In), .in1(incdec2_1_out), .out(multiplexer_1_out), .sel(plus_2));
  or or_1 (en_t, plus_2, en);
  incdec2 incdec2_1 (.in(Mon), .out(incdec2_1_out), .inc_dec_prime(not_1_out));
  not not_1 (not_1_out, inverse_inc);
  Multiplexer #(.width(16), .disabled(0), .enable("false")) multiplexer_2 (
    .in0(Mon), .in1(incdec2_1_out), .out(Out), .sel(asrt_inc));

  // Other names for the same wires on the sheet: count = plus_2

  // Notes on the sheet:
  //   asrt_inc: pull=down
  //   inverse_inc: pull=down
  //   clr: pull=down
  //   clk: pull=down
  //   en: pull=up
  //   plus_2: pull=down
endmodule

module ps_register (
  input  [3:0] flags,
  input  [15:0] word,
  input  clk,
  input  latch_word,
  input  latch_flags,
  input  ei,
  input  di,
  output [3:0] out_flags,
  output [15:0] out
);

  wire or_1_out, or_3_out, set_int_flag;
  wire [15:0] multiplexer_1_out, multiplexer_2_out;

  Multiplexer #(.width(16), .enable("false")) multiplexer_1 (
    .in0({out[15:4], flags}), .in1({ei, out[14:0]}), .out(multiplexer_1_out), .sel(set_int_flag));
  Multiplexer #(.width(16), .enable("false")) multiplexer_2 (
    .in0(multiplexer_1_out), .in1(word), .out(multiplexer_2_out), .sel(latch_word));
  or or_1 (or_1_out, latch_word, latch_flags);
  or or_2 (set_int_flag, ei, di);
  Register #(.width(16), .trigger("falling")) register_1 (
    .D(multiplexer_2_out), .en(or_3_out), .Q(out), .clk(clk));  // open: clr
  or or_3 (or_3_out, or_1_out, set_int_flag);
  Bit_Extender #(.in_width(16), .out_width(4)) bit_extender_1 (.in(out), .out(out_flags));

  // Notes on the sheet:
  //   latch_word: pull=down
  //   ei: pull=down
  //   di: pull=down
  //   word: pull=down
  //   latch_flags: pull=down
  //   flags: pull=down
  //   clk: pull=down
endmodule

module incdec2 (
  input  [15:0] in,
  input  inc_dec_prime,
  output [15:0] out
);

  wire [15:0] multiplexer_1_out;

  Multiplexer #(.width(16), .enable("false")) multiplexer_1 (
    .in0(16'hfffe), .in1(16'h2), .out(multiplexer_1_out), .sel(inc_dec_prime));
  Adder #(.width(16)) adder_1 (.a(in), .b(multiplexer_1_out), .out(out));  // open: cin, cout

  // Notes on the sheet:
  //   inc_dec_prime: pull=up
endmodule

module bus_control (
  input  sign_extend,
  input  odd_address,
  input  word,
  input  clk_no_inhibit,
  input  [15:0] from_bus,
  input  [15:0] data_in,
  output inc_address,
  output clk_inhibit,
  output phase,
  output [15:0] data_out,
  output [15:0] to_bus
);

  // verilator_component_1_0_SNAPSHOT_all_bus_control bus_control_1: pin names not known; wires that end beside it: clk_no_inhibit, 1'b0, sign_extend, odd_address, word, from_bus, data_in, phase, inc_address, clk_inhibit, data_out, to_bus

  // Notes on the sheet:
  //   data_in: pull=down
endmodule

module alu (
  input  [15:0] B,
  input  [15:0] A,
  input  [2:0] shift_count,
  input  [2:0] func,
  input  [2:0] op_type,
  input  Cin,
  output C,
  output V,
  output Z,
  output N,
  output [15:0] S
);

  // ALU_epty alu_epty_1: pin names not known; wires that end beside it: Cin, op_type, func, shift_count, A, B, {C, V, Z, N}, S

  // Notes on the sheet:
  //   B: pull=down
  //   func: pull=down
  //   Cin: pull=down
  //   op_type: pull=down
  //   A: pull=down
  //   shift_count: pull=down
endmodule

module barrel_shifter (
  input  [15:0] In,
  input  cin,
  input  [2:0] shift_type,
  input  [2:0] distance,
  output [15:0] Out,
  output cout
);

  wire [4:0] adder_1_out, bit_extender_1_out;
  wire [15:0] shifter_4_out, shifter_5_out;
  wire [16:0] shifter_1_out, shifter_2_out, shifter_3_out, shifter_6_out, shifter_7_out;

  assign bit_extender_1_out = {{2{1'b0}}, distance};  // Bit_Extender bit_extender_1
  Adder #(.width(5)) adder_1 (.a(bit_extender_1_out), .b(5'b00001), .out(adder_1_out));  // open: cin, cout
  Shifter #(.width(17)) shifter_1 (.in({{2{In[15]}}, In[14:0]}), .\dist (adder_1_out), .out(shifter_1_out));
  Shifter #(.width(17), .shift("lr")) shifter_2 (.in({In, In[0]}), .\dist (adder_1_out), .out(shifter_2_out));
  Shifter #(.width(17), .shift("ar")) shifter_3 (.in({In, In[0]}), .\dist (adder_1_out), .out(shifter_3_out));
  Shifter #(.width(16), .shift("rl")) shifter_4 (.in(In), .\dist (adder_1_out[3:0]), .out(shifter_4_out));
  Shifter #(.width(16), .shift("rr")) shifter_5 (.in(In), .\dist (adder_1_out[3:0]), .out(shifter_5_out));
  Shifter #(.width(17), .shift("rl")) shifter_6 (.in({cin, In}), .\dist (adder_1_out), .out(shifter_6_out));
  Shifter #(.width(17), .shift("rr")) shifter_7 (.in({In, cin}), .\dist (adder_1_out), .out(shifter_7_out));
  Multiplexer #(.select(3), .width(16), .enable("false")) multiplexer_1 (
    .in0(shifter_1_out[15:0]), .in1(shifter_2_out[16:1]), .in2(shifter_3_out[16:1]), .in3(shifter_4_out),
    .in4(shifter_5_out), .in5(shifter_6_out[15:0]), .in6(shifter_7_out[16:1]), .out(Out), .sel(shift_type));  // open: in7
  Multiplexer #(.select(3), .enable("false")) multiplexer_2 (
    .in0(shifter_1_out[16]), .in1(shifter_2_out[0]), .in2(shifter_3_out[0]), .in3(shifter_4_out[0]),
    .in4(shifter_5_out[15]), .in5(shifter_6_out[16]), .in6(shifter_7_out[0]), .out(cout), .sel(shift_type));  // open: in7

  // Other names for the same wires on the sheet: value[15:0] = In; type[2:0] = shift_type

  // Notes on the sheet:
  //   In: pull=down
  //   shift_type: pull=down
  //   distance: pull=down
  //   cin: pull=down
  //   shl
  //   shr
  //   shra
  //   rol
  //   ror
  //   rcl
  //   rcr
endmodule

module adder16 (
  input  Cin,
  input  [15:0] A,
  input  [15:0] B,
  output [15:0] S,
  output Cout,
  output V
);

  wire [15:0] and_1_out, and_2_out, and_3_out;
  wire [15:1] or_1_out;

  // Probe on A
  // Probe on B
  assign S = A ^ {or_1_out, Cin} ^ B;  // XOR_Gate xor_1, 16 bits wide
  assign and_1_out = B & A;  // AND_Gate and_1, 16 bits wide
  assign and_2_out = B & {or_1_out, Cin};  // AND_Gate and_2, 16 bits wide
  assign and_3_out = A & {or_1_out, Cin};  // AND_Gate and_3, 16 bits wide
  assign {Cout, or_1_out} = and_1_out | and_2_out | and_3_out;  // OR_Gate or_1, 16 bits wide
  // Probe on S
  xor xor_2 (V, or_1_out[15], Cout);

  // Notes on the sheet:
  //   B: pull=down
  //   A: pull=down
  //   Cin: pull=down
endmodule

module branch_logic (
  input  [3:0] cccc,
  input  [3:0] CVZN,
  output go
);

  // verilator_component_1_0_SNAPSHOT_all_branch_logic branch_logic_1: pin names not known; wires that end beside it: cccc, CVZN, go
endmodule

module zero16 (
  input  [15:0] in,
  output zero
);

  wire nor_1_out, nor_2_out;

  nor nor_1 (nor_1_out, in[0], in[1], in[2], in[3], in[4], in[5], in[6], in[7]);
  nor nor_2 (nor_2_out, in[8], in[9], in[10], in[11], in[12], in[13], in[14], in[15]);
  and and_1 (zero, nor_1_out, nor_2_out);
endmodule

module _2s_compliment (
  input  [15:0] In,
  output [15:0] Out
);

  wire [7:0] bit_extender_1_out;

  Bit_Extender #(.in_width(16), .out_width(8)) bit_extender_1 (.in(In), .out(bit_extender_1_out));
  assign Out = {{8{bit_extender_1_out[7]}}, bit_extender_1_out};  // Bit_Extender bit_extender_2
endmodule

module make_byte (
  input  [15:0] In,
  output [15:0] Out
);

  wire [7:0] bit_extender_1_out;

  Bit_Extender #(.in_width(16), .out_width(8)) bit_extender_1 (.in(In), .out(bit_extender_1_out));
  assign Out = {{8{1'b0}}, bit_extender_1_out};  // Bit_Extender bit_extender_2
endmodule

module bytes_swap (
  input  [15:0] In,
  output [15:0] Out
);


  assign Out = {In[7:0], In[15:8]};
endmodule
