// Logisim project simplest_scheme.circ as structural Verilog: 1 circuit, main circuit main
module main (
  input  [5:0] in_1,
  input  [15:0] bus_0
);

  wire and_2_out, button_1_out, cdm16_1_p3, cdm16_1_p4, cdm16_1_p6, cdm16_1_p7, Clock, comparator_1_eq,
       comparator_2_eq, mem, memMux, not_1_out, rd, rom_1_p4, s_r_ff_1_q, word;
  wire [5:0] adder_1_out;
  wire [6:0] cdm16_1_p12, keyboard_1_data;
  wire [8:0] cdm16_1_p12_2;
  wire [15:0] addr, cdm16_1_p13, controlled_buffer_2_out, data, kbdMemIn;

  Button button_1 (.out(button_1_out));
  Clock clock_1 (.out(Clock));
  S_R_Flip_Flop s_r_ff_1 (
    .S(button_1_out), .clk(Clock), .R(cdm16_1_p3), .Q(s_r_ff_1_q));  // open: Qn, preset, reset, en
  Adder #(.width(6)) adder_1 (.a(in_1), .b(6'b000101), .out(adder_1_out));  // open: cin, cout
  // Debugger debugger_1: pin names not known
  // Probe on cdm16_1_p4
  // Probe on cdm16_1_p7
  // Probe on cdm16_1_p6
  // cdm16 cdm16_1: pin names not known; wires that end beside it: s_r_ff_1_q, adder_1_out, cdm16_1_p3, cdm16_1_p4, Clock, cdm16_1_p6, cdm16_1_p7, mem, rd, word, addr, {cdm16_1_p12_2, cdm16_1_p12}, cdm16_1_p13
  Comparator #(.width(16)) comparator_1 (.a(addr), .b(16'hbeef), .eq(comparator_1_eq));  // open: gt, lt
  Multiplexer #(.width(16), .enable("false")) multiplexer_1 (
    .in0(controlled_buffer_2_out), .in1(kbdMemIn), .out(cdm16_1_p13), .sel(memMux));
  Comparator #(.width(16)) comparator_2 (.a(addr), .b(16'hdead), .eq(comparator_2_eq));  // open: gt, lt
  and and_1 (memMux, rd, mem, ~word, comparator_1_eq);  // AND_Gate
  and and_2 (and_2_out, ~rd, mem, ~word, comparator_2_eq);  // AND_Gate
  TTY tty_1 (.data(cdm16_1_p12), .clk(and_2_out));  // open: we, clr
  Keyboard #(.trigger("falling")) keyboard_1 (.clk(memMux), .data(keyboard_1_data));  // open: re, clr, avail
  not not_1 (not_1_out, rd);
  assign data = not_1_out ? {cdm16_1_p12_2, cdm16_1_p12} : 16'bz;  // Controlled_Buffer controlled_buffer_1
  assign controlled_buffer_2_out = rd ? data : 16'bz;  // Controlled_Buffer controlled_buffer_2
  assign kbdMemIn = {{9{1'b0}}, keyboard_1_data};  // Bit_Extender bit_extender_1
  // ROM rom_1: pin names not known; wires that end beside it: bus_0, 1'b1, 1'b1, rom_1_p4
  // RAM ram_1: pin names not known; wires that end beside it: addr, word, mem, Clock, rd, data
  // Probe on rom_1_p4
endmodule
