// Logisim project test.circ as structural Verilog: 1 circuit, main circuit main
module main (
  input  [15:0] in_1,
  input  [15:0] in_2,
  input  [2:0] op_type,
  input  [2:0] func,
  input  Cin,
  input  [15:0] A,
  input  [15:0] B,
  input  [2:0] shift_count
);

  wire button_1_out, button_2_out, registers_1_p6, registers_1_p7, undriven, undriven_2, undriven_3;

  // bus_control bus_control_1: pin names not known
  Button button_1 (.out(button_1_out));
  // Probe on undriven
  Button button_2 (.out(button_2_out));
  // Probe on undriven_2
  // branch_logic branch_logic_1: pin names not known
  // registers registers_1: pin names not known; wires that end beside it: Cin, op_type, func, shift_count, B, registers_1_p6, registers_1_p7, A
  // Probe on in_2
  // Probe on undriven_3
  // Probe on in_1
  // Probe on A
  // Probe on A
  // Probe on B
  // Probe on B
  // Probe on registers_1_p6
  // Probe on registers_1_p7
  // Probe on registers_1_p7
  // Probe on registers_1_p7
  // Probe on undriven_3
  // ALU_epty alu_epty_1: pin names not known
endmodule
